# Fritzing sketch Schema (saved by Fritzing 0.9.3b)
breadboards: 1

parts:
  active_buzzer = KY-012 Active Buzzer Module [package="Breakout board"]
  ESP-8266 = NodeMCU V1.0
  gas_detector = MQ-7 breakout
  resistor = Resistor [tolerance=±5% resistance=220 package="0603 [SMD]"]
  resistor1 = Resistor [tolerance=±5% resistance=220 package="0603 [SMD]"]
  LED = smd LED [color="Red (633nm)" package="1206 [SMD]"]
  LED1 = smd LED [color="Green (560nm)" package="1206 [SMD]"]

nets:
  N1: active_buzzer.S, ESP-8266.D3
  GND: active_buzzer.-, ESP-8266.GND, gas_detector.GND, LED.cathode, LED1.cathode
  N2: ESP-8266.D1, resistor.Pin_0
  N3: ESP-8266.D2, resistor1.Pin_1
  3V3: ESP-8266.3V3, gas_detector.VCC
  N4: ESP-8266.A0, gas_detector.AO
  N5: resistor.Pin_1, LED.anode
  N6: resistor1.Pin_0, LED1.anode

custom parts:
  KY-012 Active Buzzer Module: Active Piezoelectric Buzzer Module Keyes KY-012, it produces single-tone sound when signal is high.
  NodeMCU V1.0: ESP8266 based NodeMCU
  MQ-7 breakout: SKU: 101282
